# Fritzing sketch ECE198-CircuitDiagram-Rev3-Nov21-2024 (saved by Fritzing 0.9.5d)
circuit board: 12.8251cm x 8.51185cm
breadboards: 2

parts:
  J1 = STM32 Nucleo boards
  LED1 = LED - 5mm [color="Infrared (850nm)" package="5 mm [THT]"]
  LED2 = LED - 5mm [color="Infrared (850nm)" package="5 mm [THT]"]
  R1 = Resistor [tolerance=±5% resistance=220 package=THT]
  R2 = Resistor [tolerance=±5% resistance=220 package=THT]
  R3 = Resistor [tolerance=±5% resistance=10k package=THT]
  R4 = Resistor [tolerance=±5% resistance=10k package=THT]
  R5 = Resistor [tolerance=±5% resistance=10k package=THT]
  R6 = Resistor [tolerance=±5% resistance=10k package=THT]
  J2 = STM32 Nucleo boards
  Buzzer = Piezo Speaker
  LCD1 = LCD screen
  IC2 = PCF8574 [package="DIP16 [THT]"]
  POT1 = POT [package=alps_pot]
  R7 = Resistor [tolerance=±5% resistance=1k package=THT]
  IC1 = L293D [package=THT]
  Solenoid_1 = Solenoid
  Solenoid_2 = Solenoid
  PD1 = S1133 Si Photodiode [package="8mm Ceramic [THT]"]
  PD2 = S1133 Si Photodiode [package="8mm Ceramic [THT]"]
  PD3 = S1133 Si Photodiode [package="8mm Ceramic [THT]"]
  PD4 = S1133 Si Photodiode [package="8mm Ceramic [THT]"]
  R8 = Resistor [tolerance=±5% resistance=10k package=THT]
  R9 = Resistor [tolerance=±5% resistance=10k package=THT]
  Q1 = NPN-Transistor [package="TO92 [THT]"]

nets:
  N1: J1.A0, R6.Pin_1, PD4.anode
  N2: J1.A1, R5.Pin_1, PD3.anode
  N3: J1.A2, R4.Pin_1, PD2.anode
  N4: J1.A3, R3.Pin_1, PD1.anode
  GND: J1.GND, R1.Pin_1, R2.Pin_1, R3.Pin_0, R4.Pin_0, R5.Pin_0, R6.Pin_0, J2.GND, Buzzer.pin1, LCD1.VSS, LCD1.LED-, IC2.GND, POT1.A, IC1.0V
  N5: J1.D9_PWM, LED1.anode
  N6: J1.D10_PWM/SS, IC1.In_4
  N7: J1.D11_PWM/MOSI, IC1.In_3
  N8: J1.D0/RX, J2.D1/TX
  N9: J1.D1/TX, J2.D0/RX
  N10: J1.D2, IC1.In_2
  N11: J1.D3_PWM, IC1.In_1
  N12: J1.D6_PWM, LED2.anode
  N13: J1.3V3, PD1.cathode, PD2.cathode, PD3.cathode, PD4.cathode
  N14: J1.5V, IC1.Enable_1, IC1.+Vmotor, IC1.Enable_2, IC1.+V
  N15: LED1.cathode, R1.Pin_0
  N16: LED2.cathode, R2.Pin_0
  N17: J2.A0, R7.Pin_0
  5V: J2.SWDIO, J2.5V, LCD1.VDD, LCD1.LED+, IC2.VCC, POT1.E, R8.Pin_0, R9.Pin_0, Q1.C
  N18: J2.A4/SDA, IC2.SDA, R8.Pin_1
  N19: J2.A5/SCL, IC2.SCL, R9.Pin_1
  N20: Buzzer.pin2, Q1.E
  N21: LCD1.V0, POT1.S
  N22: LCD1.RS, IC2.P0
  N23: LCD1.R/W, IC2.P1
  N24: LCD1.E, IC2.P2
  N25: LCD1.DB4, IC2.P4
  N26: LCD1.DB5, IC2.P5
  N27: LCD1.DB6, IC2.P6
  N28: LCD1.DB7, IC2.P7
  N29: R7.Pin_1, Q1.B
  N30: IC1.Out_1_(_Controlled_by_Enable_1_), Solenoid_2.pin2
  N31: IC1.Out_2_(_Controlled_by_Enable_1_), Solenoid_2.pin1
  N32: IC1.Out_3_(_Controlled_by_Enable_2_), Solenoid_1.pin2
  N33: IC1.Out_4_(_Controlled_by_Enable_2_), Solenoid_1.pin1

notes:
  Circuit for Dashboard device, connected to Measurement device using UART
  Circuit for Measurement device, connected to Dashboard device using UART
  Circuit pictorial diagram for ECE198 Group 26 (rev. 2)
  Circuit Schematic for ECE198 Group 26 (rev. 2)
  Left: circuit for measurement device
  Right: circuit for dashboard device
  The only shared connections between the two circuits are TX/RX, RX/TX, GND, which are colored
  Label legend:
  PD -> Photodiode
  POT -> Potentiometer
  LCD -> Liquid Crystal Display
  PCF8574 -> 8-bit I/O Expander, I2C
  L293D -> Quad H-Bridge motor driver
